# Fritzing sketch Second Vehicle (saved by Fritzing 1.0.6)

parts:
  S1 = H-Bridge with L298N
  HC-SR04_Sensor_1 = HC-SR04 Ultrasonic Distance Sensor
  M1 = gear-motor
  M2 = gear-motor
  M3 = gear-motor  # not connected
  M4 = gear-motor  # not connected
  A1 = Raspberry Pi 5  # not connected
  Part1 = Arduino Nano (Rev3.0) (ICSP)
  VCC2 = Battery [internal_resistance=0.1Ω]
  U1 = TCM8240MD [package=tcm8240md]  # not connected

nets:
  N1: S1.12V, VCC2.+
  GND: S1.GND, HC-SR04_Sensor_1.GND, Part1.GND, VCC2.-
  5V: S1.5V, HC-SR04_Sensor_1.VCC, Part1.5V
  N2: S1.ENA, S1.ENA-5V
  N3: S1.IN1, Part1.D3
  N4: S1.IN2, Part1.D4
  N5: S1.IN3, Part1.D5
  N6: S1.IN4, Part1.D6
  N7: S1.ENB, S1.ENB-5V
  N8: S1.M1-02, M1.pin_2
  N9: S1.M2-01, M2.pin_2
  N10: S1.M2-02, M2.pin_1
  N11: HC-SR04_Sensor_1.TRIG, Part1.D8
  N12: HC-SR04_Sensor_1.ECHO, Part1.D7

custom parts:
  H-Bridge with L298N: h-bridge
  Raspberry Pi 5: The RPi5, a faster version of the awesome Raspberry Pi4B ARM Board with 40 pin gpio.
