# Fritzing sketch main vehicle blocks (saved by Fritzing 1.0.6)

parts:
  S1 = H-Bridge with L298N
  Part1 = Arduino Uno (Rev3) - ICSP
  HC-SR04_Sensor_1 = HC-SR04 Ultrasonic Distance Sensor
  J1 = Basic Servo
  Mod1 = Arduino Sensor Shield v5.0
  M1 = gear-motor
  M2 = gear-motor
  M3 = gear-motor  # not connected
  M4 = gear-motor  # not connected
  VCC1 = 4 x AAA Battery Mount [internal_resistance=0.1Ω]

nets:
  N1: S1.12V, VCC1.+
  GND: S1.GND, HC-SR04_Sensor_1.GND, J1.gnd, Mod1.URF01-GND, Mod1.GND, Mod1.12-G, Mod1.ParallelLCD-GND, VCC1.-
  VCC: S1.5V, Part1.RESET, HC-SR04_Sensor_1.VCC, J1.vcc, Mod1.VCC, Mod1.URF01-VCC, Mod1.BLUETOOTH-VCC, Mod1.12-V, Mod1.ParallelLCD-VCC
  N2: S1.ENA, S1.ENA-5V
  N3: S1.IN1, Mod1.SD-D11, Mod1.11-S
  N4: S1.IN2, Mod1.10-S, Mod1.ParallelLCD-D10
  N5: S1.IN3, Mod1.9-S, Mod1.ParallelLCD-D9
  N6: S1.IN4, Mod1.8-S, Mod1.ParallelLCD-D8
  N7: S1.ENB, S1.ENB-5V
  N8: S1.M1-02, M1.pin_2
  N9: S1.M2-01, M2.pin_2
  N10: S1.M2-02, M2.pin_1
  N11: HC-SR04_Sensor_1.TRIG, Mod1.URF01-A0
  N12: HC-SR04_Sensor_1.ECHO, Mod1.URF01-A1
  N13: J1.pulse, Mod1.12-S, Mod1.ParallelLCD-D12

custom parts:
  H-Bridge with L298N: h-bridge
